// Logisim project Computer.circ as structural Verilog: 16 circuits, main circuit main
module main (
);

  wire buscontrollera_1_mb_ld, buscontrollera_1_ra_mbld, buscontrollera_1_ra_th, buscontrollera_1_ra_tl,
       buscontrollera_1_ra_txld, buscontrollera_1_rb_mbld, buscontrollera_1_rb_th, buscontrollera_1_rb_tl,
       buscontrollera_1_rb_txld, buscontrollera_1_rc_lh, buscontrollera_1_rc_mbld, buscontrollera_1_rc_tl,
       buscontrollera_1_rc_txld, buscontrollera_1_rd_mbld, buscontrollera_1_rd_th, buscontrollera_1_rd_tl,
       buscontrollera_1_rd_txld, buscontrollera_1_st_pop, buscontrollera_1_st_push, clockunit_1_clock_out,
       dipswitch_1_sw1, dipswitch_1_sw2, not_1_out, or_1_out, pipelinestage0_1_mem_read,
       pipelinestage0_1_pc_inc, pipelinestage0_1_pc_oadb, pipelinestage1_1_alu_disp, pipelinestage1_1_pc_inc,
       pipelinestage1_1_stall_0, pull_resistor_6_node, switch_1_p3;
  wire [1:0] buscontrollera_1_tx_load, or_2_out, pipelinestage1_1_mb_inst;
  wire [3:0] pipelinestage1_1_alu_inst;
  wire [6:0] pull_resistor_5_node;
  wire [7:0] memorybridge_1_otfrl_bus, memoryunit_1_data_bus, pipelinestage0_1_inst_out,
       pipelinestage1_1_txb_inst;
  wire [15:0] addressregister_1_addr_bus, addressregister_1_tfer_buso;

  DipSwitch #(.number(2)) dipswitch_1 (.sw1(dipswitch_1_sw1), .sw2(dipswitch_1_sw2));
  not not_1 (not_1_out, pipelinestage0_1_mem_read);
  ClockUnit clockunit_1 (
    .MANUAL_CLOCK(dipswitch_1_sw1), .CLOCK_SELECT(dipswitch_1_sw2), .CLOCK_OUT(clockunit_1_clock_out));  // open: INV_CLOCK_OUT
  AddressRegister addressregister_1 (
    .TFER_BUS(addressregister_1_tfer_buso), .INC(or_1_out), .OADDR(pipelinestage0_1_pc_oadb),
    .CLOCK(clockunit_1_clock_out), .ADDR_BUS(addressregister_1_addr_bus),
    .TFER_BUSO(addressregister_1_tfer_buso));  // open: DEC, OTFER, Load
  AddressRegister addressregister_2 (
    .TFER_BUS(addressregister_1_tfer_buso), .OTFER(buscontrollera_1_tx_load[1]),
    .Load(buscontrollera_1_tx_load[0]), .CLOCK(clockunit_1_clock_out), .ADDR_BUS(addressregister_1_addr_bus),
    .TFER_BUSO(addressregister_1_tfer_buso));  // open: INC, DEC, OADDR
  AddressRegister addressregister_3 (
    .TFER_BUS(addressregister_1_tfer_buso), .CLOCK(clockunit_1_clock_out),
    .ADDR_BUS(addressregister_1_addr_bus), .TFER_BUSO(addressregister_1_tfer_buso));  // open: INC, DEC, OADDR, OTFER, Load
  MemoryUnit memoryunit_1 (
    .ADDR_BUS(addressregister_1_addr_bus), .RWB(not_1_out), .CLOCK(clockunit_1_clock_out),
    .DATA_BUS(memoryunit_1_data_bus));
  MemoryBridge memorybridge_1 (
    .LOAD(or_2_out[0]), .STORE(or_2_out[1]), .TFRL_BUS(memorybridge_1_otfrl_bus),
    .DATA_BUS(memoryunit_1_data_bus), .ODATA_BUS(memoryunit_1_data_bus), .OTFRL_BUS(memorybridge_1_otfrl_bus));
  // Probe on memoryunit_1_data_bus
  Pull_Resistor pull_resistor_1 (.node(memoryunit_1_data_bus));
  // Probe on addressregister_1_addr_bus
  Pull_Resistor pull_resistor_2 (.node(addressregister_1_addr_bus));
  // Probe on addressregister_1_tfer_buso
  Pull_Resistor pull_resistor_3 (.node(addressregister_1_tfer_buso));
  // Probe on memorybridge_1_otfrl_bus
  Pull_Resistor pull_resistor_4 (.node(memorybridge_1_otfrl_bus));
  GeneralPurposeRegister generalpurposeregister_1 (
    .TFRL_BUS(addressregister_1_tfer_buso[15:8]), .TFRH_BUS(addressregister_1_tfer_buso[7:0]),
    .MAIN_BUS(memorybridge_1_otfrl_bus), .TFRL(buscontrollera_1_ra_tl), .TFRH(buscontrollera_1_ra_th),
    .TXLD(buscontrollera_1_ra_txld), .CLOCK(clockunit_1_clock_out), .MBLD(buscontrollera_1_ra_mbld),
    .TFRH_BUSO(addressregister_1_tfer_buso[7:0]), .TFRL_BUSO(addressregister_1_tfer_buso[15:8]));
  GeneralPurposeRegister generalpurposeregister_2 (
    .TFRL_BUS(addressregister_1_tfer_buso[15:8]), .TFRH_BUS(addressregister_1_tfer_buso[7:0]),
    .MAIN_BUS(memorybridge_1_otfrl_bus), .TFRL(buscontrollera_1_rb_tl), .TFRH(buscontrollera_1_rb_th),
    .TXLD(buscontrollera_1_rb_txld), .CLOCK(clockunit_1_clock_out), .MBLD(buscontrollera_1_rb_mbld),
    .TFRH_BUSO(addressregister_1_tfer_buso[7:0]), .TFRL_BUSO(addressregister_1_tfer_buso[15:8]));
  GeneralPurposeRegister generalpurposeregister_3 (
    .TFRL_BUS(addressregister_1_tfer_buso[15:8]), .TFRH_BUS(addressregister_1_tfer_buso[7:0]),
    .MAIN_BUS(memorybridge_1_otfrl_bus), .TFRL(buscontrollera_1_rc_tl), .TFRH(buscontrollera_1_rc_lh),
    .TXLD(buscontrollera_1_rc_txld), .CLOCK(clockunit_1_clock_out), .MBLD(buscontrollera_1_rc_mbld),
    .TFRH_BUSO(addressregister_1_tfer_buso[7:0]), .TFRL_BUSO(addressregister_1_tfer_buso[15:8]));
  GeneralPurposeRegister generalpurposeregister_4 (
    .TFRL_BUS(addressregister_1_tfer_buso[15:8]), .TFRH_BUS(addressregister_1_tfer_buso[7:0]),
    .MAIN_BUS(memorybridge_1_otfrl_bus), .TFRL(buscontrollera_1_rd_tl), .TFRH(buscontrollera_1_rd_th),
    .TXLD(buscontrollera_1_rd_txld), .CLOCK(clockunit_1_clock_out), .MBLD(buscontrollera_1_rd_mbld),
    .TFRH_BUSO(addressregister_1_tfer_buso[7:0]), .TFRL_BUSO(addressregister_1_tfer_buso[15:8]));
  Stack stack_1 (
    .TFER_BUS(addressregister_1_tfer_buso), .CLOCK(clockunit_1_clock_out), .PUSH(buscontrollera_1_st_push),
    .POP(buscontrollera_1_st_pop), .OTFER_BUS(addressregister_1_tfer_buso));
  ArithmeticLogicUnit arithmeticlogicunit_1 (
    .TFRL_BUS(addressregister_1_tfer_buso[15:8]), .TFRH_BUS(addressregister_1_tfer_buso[7:0]),
    .ALU_CTL_BUS(pipelinestage1_1_alu_inst), .CLOCK(clockunit_1_clock_out),
    .MAIN_BUS(memorybridge_1_otfrl_bus));  // open: FLAGS_IN, FLAGS_OUT
  Pull_Resistor pull_resistor_5 (.node(pull_resistor_5_node));
  PipelineStage0 pipelinestage0_1 (
    .INST_IN(memoryunit_1_data_bus), .CLOCK(clockunit_1_clock_out), .STALL(pipelinestage1_1_stall_0),
    .PC_OADB(pipelinestage0_1_pc_oadb), .PC_INC(pipelinestage0_1_pc_inc),
    .MEM_READ(pipelinestage0_1_mem_read), .INST_OUT(pipelinestage0_1_inst_out));
  PipelineStage1 pipelinestage1_1 (
    .INST_IN(pipelinestage0_1_inst_out), .CLOCK(clockunit_1_clock_out), .STALL(pull_resistor_6_node),
    .FLAGS(pull_resistor_5_node), .STALL_0(pipelinestage1_1_stall_0), .PC_INC(pipelinestage1_1_pc_inc),
    .TXB_INST(pipelinestage1_1_txb_inst), .ALU_DISP(pipelinestage1_1_alu_disp),
    .MB_INST(pipelinestage1_1_mb_inst), .ALU_INST(pipelinestage1_1_alu_inst));  // open: INST_OUT, MB_LOAD
  or or_1 (or_1_out, pipelinestage0_1_pc_inc, pipelinestage1_1_pc_inc);
  Pull_Resistor pull_resistor_6 (.node(pull_resistor_6_node));
  // Switch switch_1: pin names not known; wires that end beside it: pull_resistor_6_node, 1'b1, switch_1_p3
  BusControllerA buscontrollera_1 (
    .TXB_INST(pipelinestage1_1_txb_inst), .ALU_DISP(pipelinestage1_1_alu_disp),
    .MB_INST(pipelinestage1_1_mb_inst), .ST_PUSH(buscontrollera_1_st_push),
    .TX_LOAD(buscontrollera_1_tx_load[0]), .TX_OTXB(buscontrollera_1_tx_load[1]),
    .ST_POP(buscontrollera_1_st_pop), .MB_LD(buscontrollera_1_mb_ld), .MB_EN(or_2_out[1]),
    .RA_MBLD(buscontrollera_1_ra_mbld), .RA_TXLD(buscontrollera_1_ra_txld), .RA_TL(buscontrollera_1_ra_tl),
    .RA_TH(buscontrollera_1_ra_th), .RB_MBLD(buscontrollera_1_rb_mbld), .RB_TXLD(buscontrollera_1_rb_txld),
    .RB_TL(buscontrollera_1_rb_tl), .RB_TH(buscontrollera_1_rb_th), .RC_MBLD(buscontrollera_1_rc_mbld),
    .RC_TXLD(buscontrollera_1_rc_txld), .RC_TL(buscontrollera_1_rc_tl), .RC_LH(buscontrollera_1_rc_lh),
    .RD_MBLD(buscontrollera_1_rd_mbld), .RD_TXLD(buscontrollera_1_rd_txld), .RD_TL(buscontrollera_1_rd_tl),
    .RD_TH(buscontrollera_1_rd_th));  // open: FG_LD, FG_EN
  Pull_Resistor pull_resistor_7 (.node(switch_1_p3));
  or or_2 (or_2_out[0], switch_1_p3, buscontrollera_1_mb_ld);

  // Notes on the sheet:
  //   Program Counter
  //   Transfer Register
  //   Interrupt Address Register
  //   DATA
  //   ADDR
  //   TFER
  //   MAIN
  //   General Purpose Registers
  //   FLAGS REGISTER NIY
  //   Pipeline
endmodule

module ClockUnit (
  input  MANUAL_CLOCK,
  input  CLOCK_SELECT,
  output CLOCK_OUT,
  output INV_CLOCK_OUT
);

  wire and_1_out, and_2_out, clock_1_out, not_1_out;

  Clock clock_1 (.out(clock_1_out));
  not not_1 (not_1_out, CLOCK_SELECT);
  Pull_Resistor pull_resistor_1 (.node(CLOCK_SELECT));
  and and_1 (and_1_out, clock_1_out, not_1_out);
  and and_2 (and_2_out, MANUAL_CLOCK, CLOCK_SELECT);
  LED led_1 (.in(CLOCK_OUT));
  LED led_2 (.in(INV_CLOCK_OUT));
  or or_1 (CLOCK_OUT, and_1_out, and_2_out);
  not not_2 (INV_CLOCK_OUT, CLOCK_OUT);
endmodule

module AddressRegister (
  input  [15:0] TFER_BUS,
  input  INC,
  input  DEC,
  input  OADDR,
  input  OTFER,
  input  Load,
  input  CLOCK,
  output [15:0] ADDR_BUS,
  output [15:0] TFER_BUSO
);

  wire button_1_out, not_1_out, not_2_out, or_1_out, or_2_out;
  wire [15:0] adder_1_out, controlled_buffer_1_out, controlled_buffer_2_out, register_1_q;

  assign controlled_buffer_1_out = Load ? TFER_BUS : 16'bz;  // Controlled_Buffer controlled_buffer_1
  or or_1 (or_1_out, INC, DEC);
  assign controlled_buffer_2_out = INC ? 16'h1 : 16'bz;  // Controlled_Buffer controlled_buffer_2
  not not_1 (not_1_out, INC);
  assign controlled_buffer_2_out = not_1_out ? {16{1'b1}} : 16'bz;  // Controlled_Buffer controlled_buffer_3
  Register #(.width(16)) register_1 (
    .D(controlled_buffer_1_out), .en(or_2_out), .clk(not_2_out), .Q(register_1_q), .clr(button_1_out));
  or or_2 (or_2_out, or_1_out, Load);
  not not_2 (not_2_out, CLOCK);
  assign controlled_buffer_1_out = or_1_out ? adder_1_out : 16'bz;  // Controlled_Buffer controlled_buffer_4
  Adder #(.width(16)) adder_1 (.a(controlled_buffer_2_out), .b(register_1_q), .out(adder_1_out));  // open: cin, cout
  Button button_1 (.out(button_1_out));
  assign TFER_BUSO = OTFER ? register_1_q : 16'bz;  // Controlled_Buffer controlled_buffer_5
  assign ADDR_BUS = OADDR ? register_1_q : 16'bz;  // Controlled_Buffer controlled_buffer_6
endmodule

module GeneralPurposeRegister (
  input  [7:0] TFRL_BUS,
  input  [7:0] TFRH_BUS,
  input  [7:0] MAIN_BUS,
  input  TFRL,
  input  TFRH,
  input  TXLD,
  input  CLOCK,
  input  MBLD,
  output [7:0] TFRL_BUSO,
  output [7:0] TFRH_BUSO
);

  wire and_1_out, and_2_out, not_1_out, not_2_out, not_3_out, not_4_out, or_1_out;
  wire [7:0] controlled_buffer_1_out, controlled_buffer_3_out, controlled_buffer_5_out, register_1_q;

  not not_1 (not_1_out, TXLD);
  and and_1 (and_1_out, TFRL, not_1_out);
  or or_1 (or_1_out, TXLD, MBLD);
  and and_2 (and_2_out, not_1_out, TFRH);
  assign controlled_buffer_1_out = TFRL ? TFRL_BUS : 8'bz;  // Controlled_Buffer controlled_buffer_1
  assign controlled_buffer_1_out = TFRH ? TFRH_BUS : 8'bz;  // Controlled_Buffer controlled_buffer_2
  not not_2 (not_2_out, MBLD);
  assign controlled_buffer_3_out = MBLD ? MAIN_BUS : 8'bz;  // Controlled_Buffer controlled_buffer_3
  assign controlled_buffer_3_out = not_2_out ? controlled_buffer_1_out : 8'bz;  // Controlled_Buffer controlled_buffer_4
  Register register_1 (.D(controlled_buffer_5_out), .en(or_1_out), .clk(not_3_out), .Q(register_1_q));  // open: clr
  assign controlled_buffer_5_out = or_1_out ? controlled_buffer_3_out : 8'bz;  // Controlled_Buffer controlled_buffer_5
  not not_3 (not_3_out, CLOCK);
  not not_4 (not_4_out, MBLD);
  assign TFRH_BUSO = and_2_out ? register_1_q : 8'bz;  // Controlled_Buffer controlled_buffer_6
  assign TFRL_BUSO = and_1_out ? register_1_q : 8'bz;  // Controlled_Buffer controlled_buffer_7
endmodule

module ArithmeticLogicUnit (
  input  [7:0] TFRL_BUS,
  input  [7:0] TFRH_BUS,
  input  [3:0] ALU_CTL_BUS,
  input  CLOCK,
  input  [7:0] FLAGS_IN,
  output [7:0] MAIN_BUS,
  output [7:0] FLAGS_OUT
);

  wire aludecode_1_add_en, aludecode_1_logic_en, multiplexer_1_out, multiplexer_2_out;
  wire [1:0] aludecode_1_carry_sel, aludecode_1_shift_sel;
  wire [3:0] aludecode_1_bitwise_sel;
  wire [7:0] adder_1_out, logicunit_1_lu_out;

  Multiplexer #(.select(2)) multiplexer_1 (
    .in0(1'b0), .in1(FLAGS_IN[1]), .in2(1'b1), .in3(1'b0), .out(multiplexer_1_out),
    .sel(aludecode_1_carry_sel));
  Multiplexer #(.select(2)) multiplexer_2 (
    .in0(1'b0), .in1(FLAGS_IN[1]), .in2(1'b1), .in3(1'b0), .out(multiplexer_2_out),
    .sel(aludecode_1_carry_sel));
  Adder adder_1 (.a(TFRL_BUS), .b(TFRH_BUS), .out(adder_1_out), .cin(multiplexer_2_out), .cout(FLAGS_OUT[0]));
  LogicUnit logicunit_1 (.OP_LUT(aludecode_1_bitwise_sel), .LHS(TFRL_BUS), .RHS(TFRH_BUS), .LU_OUT(logicunit_1_lu_out));
  ShiftUnit shiftunit_1 (
    .SFT_CODE(aludecode_1_shift_sel), .CARRY_IN(multiplexer_1_out), .LHS(TFRL_BUS), .CARRY_OUT(FLAGS_OUT[0]),
    .SU_OUT(MAIN_BUS));
  ALUDecode aludecode_1 (
    .ALU_INST(ALU_CTL_BUS), .LOGIC_EN(aludecode_1_logic_en), .ADD_EN(aludecode_1_add_en),
    .CARRY_SEL(aludecode_1_carry_sel), .SHIFT_SEL(aludecode_1_shift_sel),
    .BITWISE_SEL(aludecode_1_bitwise_sel));
  assign MAIN_BUS = aludecode_1_logic_en ? logicunit_1_lu_out : 8'bz;  // Controlled_Buffer controlled_buffer_1
  assign MAIN_BUS = aludecode_1_add_en ? adder_1_out : 8'bz;  // Controlled_Buffer controlled_buffer_2
endmodule

module ALUDecode (
  input  [3:0] ALU_INST,
  output [1:0] CARRY_SEL,
  output [1:0] SHIFT_SEL,
  output [3:0] BITWISE_SEL,
  output LOGIC_EN,
  output ADD_EN
);

  wire xor_1_out;

  ROM #(.addrWidth(4)) rom_1 (.addr(ALU_INST), .data({CARRY_SEL, SHIFT_SEL, BITWISE_SEL}));
  xor xor_1 (xor_1_out, ALU_INST[1], ALU_INST[2]);
  not not_1 (ADD_EN, ALU_INST[3]);
  and and_1 (LOGIC_EN, ALU_INST[3], xor_1_out);

  // Notes on the sheet:
  //   contents of rom_1 (hex, n*v repeats v):
  //   c 4c 83 43 80 40 f 4f 10 20 33 38 3e 36
endmodule

module LogicUnit (
  input  [7:0] LHS,
  input  [7:0] RHS,
  input  [3:0] OP_LUT,
  output [7:0] LU_OUT
);

  Multiplexer #(.select(2)) multiplexer_1 (
    .in0(OP_LUT[0]), .in1(OP_LUT[1]), .in2(OP_LUT[2]), .in3(OP_LUT[3]), .out(LU_OUT[0]),
    .sel({RHS[0], LHS[0]}));
  Multiplexer #(.select(2)) multiplexer_2 (
    .in0(OP_LUT[0]), .in1(OP_LUT[1]), .in2(OP_LUT[2]), .in3(OP_LUT[3]), .out(LU_OUT[1]),
    .sel({RHS[1], LHS[1]}));
  Multiplexer #(.select(2)) multiplexer_3 (
    .in0(OP_LUT[0]), .in1(OP_LUT[1]), .in2(OP_LUT[2]), .in3(OP_LUT[3]), .out(LU_OUT[2]),
    .sel({RHS[2], LHS[2]}));
  Multiplexer #(.select(2)) multiplexer_4 (
    .in0(OP_LUT[0]), .in1(OP_LUT[1]), .in2(OP_LUT[2]), .in3(OP_LUT[3]), .out(LU_OUT[3]),
    .sel({RHS[3], LHS[3]}));
  Multiplexer #(.select(2)) multiplexer_5 (
    .in0(OP_LUT[0]), .in1(OP_LUT[1]), .in2(OP_LUT[2]), .in3(OP_LUT[3]), .out(LU_OUT[4]),
    .sel({RHS[4], LHS[4]}));
  Multiplexer #(.select(2)) multiplexer_6 (
    .in0(OP_LUT[0]), .in1(OP_LUT[1]), .in2(OP_LUT[2]), .in3(OP_LUT[3]), .out(LU_OUT[5]),
    .sel({RHS[5], LHS[5]}));
  Multiplexer #(.select(2)) multiplexer_7 (
    .in0(OP_LUT[0]), .in1(OP_LUT[1]), .in2(OP_LUT[2]), .in3(OP_LUT[3]), .out(LU_OUT[6]),
    .sel({RHS[6], LHS[6]}));
  Multiplexer #(.select(2)) multiplexer_8 (
    .in0(OP_LUT[0]), .in1(OP_LUT[1]), .in2(OP_LUT[2]), .in3(OP_LUT[3]), .out(LU_OUT[7]),
    .sel({RHS[7], LHS[7]}));
endmodule

module ShiftUnit (
  input  [7:0] LHS,
  input  [1:0] SFT_CODE,
  input  CARRY_IN,
  output [7:0] SU_OUT,
  output CARRY_OUT
);

  wire demultiplexer_1_out0, demultiplexer_1_out1, demultiplexer_1_out2, demultiplexer_1_out3;

  Demultiplexer #(.select(2)) demultiplexer_1 (
    .out0(demultiplexer_1_out0), .out1(demultiplexer_1_out1), .out2(demultiplexer_1_out2),
    .out3(demultiplexer_1_out3), .in(1'b1), .sel(SFT_CODE));
  assign SU_OUT = demultiplexer_1_out3 ? {8{1'b0}} : 8'bz;  // Controlled_Buffer controlled_buffer_1
  assign SU_OUT = demultiplexer_1_out2 ? {CARRY_IN, LHS[7:1]} : 8'bz;  // Controlled_Buffer controlled_buffer_2
  assign SU_OUT = demultiplexer_1_out1 ? {LHS[6:1], LHS[7], CARRY_IN} : 8'bz;  // Controlled_Buffer controlled_buffer_3
  assign SU_OUT = 1'b0 ? {LHS[7:1], LHS[7]} : 8'bz;  // Controlled_Buffer controlled_buffer_4

  assign CARRY_OUT = LHS[7];
  assign LHS[0] = LHS[7];
endmodule

module MemoryUnit (
  input  [15:0] ADDR_BUS,
  input  RWB,
  input  CLOCK,
  output [7:0] DATA_BUS
);

  wire not_1_out;
  wire [7:0] ram_1_dout, undriven;

  ROM #(.addrWidth(16)) rom_1 (.addr(ADDR_BUS), .data(DATA_BUS));
  RAM #(.addrWidth(16)) ram_1 (
    .addr(ADDR_BUS), .we(RWB), .oe(not_1_out), .clk(CLOCK), .din(undriven), .dout(ram_1_dout));
  not not_1 (not_1_out, RWB);

  // Notes on the sheet:
  //   contents of rom_1 (hex, n*v repeats v):
  //   40 40 41 41 41 50
endmodule

module MemoryBridge (
  input  [7:0] DATA_BUS,
  input  [7:0] TFRL_BUS,
  input  LOAD,
  input  STORE,
  output [7:0] OTFRL_BUS,
  output [7:0] ODATA_BUS
);

  assign OTFRL_BUS = LOAD ? DATA_BUS : 8'bz;  // Controlled_Buffer controlled_buffer_1
  assign ODATA_BUS = STORE ? TFRL_BUS : 8'bz;  // Controlled_Buffer controlled_buffer_2
endmodule

module FlagsRegister (
  input  OE,
  input  [7:0] FLAGS,
  input  UPD,
  input  CLOCK,
  output [7:0] TFRL_BUS,
  output [7:0] OFLAGS
);

  Register register_1 (.D(FLAGS), .en(UPD), .clk(CLOCK), .Q(OFLAGS));  // open: clr
  LED led_1 (.in(OFLAGS[7]));
  LED led_2 (.in(OFLAGS[6]));
  LED led_3 (.in(OFLAGS[5]));
  assign TFRL_BUS = OE ? OFLAGS : 8'bz;  // Controlled_Buffer controlled_buffer_1
  LED led_4 (.in(OFLAGS[4]));
  LED led_5 (.in(OFLAGS[3]));
  LED led_6 (.in(OFLAGS[2]));
  LED led_7 (.in(OFLAGS[1]));
  LED led_8 (.in(OFLAGS[0]));
endmodule

module Stack (
  input  [15:0] TFER_BUS,
  input  CLOCK,
  input  PUSH,
  input  POP,
  output [15:0] OTFER_BUS
);

  wire d_ff_1_q;
  wire [7:0] ram_1_dout, ram_2_dout, stackpointer_1_addr;

  StackPointer stackpointer_1 (.INC(PUSH), .DEC(POP), .CLOCK(CLOCK), .ADDR(stackpointer_1_addr));
  D_Flip_Flop d_ff_1 (.D(POP), .clk(CLOCK), .Q(d_ff_1_q));  // open: Qn, preset, reset
  RAM ram_1 (.addr(stackpointer_1_addr), .we(PUSH), .oe(POP), .clk(CLOCK), .din(TFER_BUS[7:0]), .dout(ram_1_dout));
  RAM ram_2 (.addr(stackpointer_1_addr), .we(PUSH), .oe(POP), .clk(CLOCK), .din(TFER_BUS[15:8]), .dout(ram_2_dout));
  assign OTFER_BUS = d_ff_1_q ? {ram_2_dout, ram_1_dout} : 16'bz;  // Controlled_Buffer controlled_buffer_1
endmodule

module StackPointer (
  input  INC,
  input  DEC,
  input  CLOCK,
  output [7:0] ADDR
);

  wire not_1_out, not_2_out, or_1_out;
  wire [7:0] adder_1_out, controlled_buffer_1_out, controlled_buffer_3_out;

  or or_1 (or_1_out, INC, DEC);
  assign controlled_buffer_1_out = INC ? 8'h1 : 8'bz;  // Controlled_Buffer controlled_buffer_1
  not not_1 (not_1_out, INC);
  assign controlled_buffer_1_out = not_1_out ? {8{1'b1}} : 8'bz;  // Controlled_Buffer controlled_buffer_2
  Register register_1 (.D(controlled_buffer_3_out), .en(or_1_out), .clk(not_2_out), .Q(ADDR));  // open: clr
  not not_2 (not_2_out, CLOCK);
  assign controlled_buffer_3_out = or_1_out ? adder_1_out : 8'bz;  // Controlled_Buffer controlled_buffer_3
  Adder adder_1 (.a(controlled_buffer_1_out), .b(ADDR), .out(adder_1_out));  // open: cin, cout
endmodule

module BusControllerA (
  input  [7:0] TXB_INST,
  input  ALU_DISP,
  input  [1:0] MB_INST,
  output MB_LD,
  output MB_EN,
  output FG_LD,
  output FG_EN,
  output RA_MBLD,
  output RA_TXLD,
  output RA_TL,
  output RA_TH,
  output RB_MBLD,
  output RB_TXLD,
  output RB_TL,
  output RB_TH,
  output RC_MBLD,
  output RC_TXLD,
  output RC_TL,
  output RC_LH,
  output RD_MBLD,
  output RD_TXLD,
  output RD_TL,
  output RD_TH,
  output ST_POP,
  output ST_PUSH,
  output TX_LOAD,
  output TX_OTXB
);

  wire and_1_out, and_2_out, and_3_out, controlled_buffer_5_out, controlled_buffer_6_out,
       controlled_buffer_7_out, controlled_buffer_8_out, demultiplexer_1_out0, demultiplexer_1_out1,
       demultiplexer_1_out2, demultiplexer_1_out3, demultiplexer_3_out0, demultiplexer_3_out1,
       demultiplexer_3_out2, demultiplexer_3_out3, demultiplexer_4_out0, demultiplexer_4_out1,
       demultiplexer_4_out2, demultiplexer_4_out3, demultiplexer_5_out0, demultiplexer_5_out1,
       demultiplexer_6_out0, demultiplexer_6_out1, demultiplexer_9_out0, demultiplexer_9_out1,
       demultiplexer_9_out2, demultiplexer_9_out3, demultiplexer_10_out0, demultiplexer_10_out1,
       demultiplexer_10_out2, demultiplexer_10_out3, or_1_out, or_2_out, or_3_out, or_4_out, or_5_out,
       or_6_out, or_9_out, or_12_out;
  wire [5:0] pull_resistor_1_node, pull_resistor_2_node, pull_resistor_3_node, pull_resistor_4_node;

  Demultiplexer #(.select(2)) demultiplexer_1 (
    .out0(demultiplexer_1_out0), .out1(demultiplexer_1_out1), .out2(demultiplexer_1_out2),
    .out3(demultiplexer_1_out3), .in(1'b1), .sel(TXB_INST[7:6]));
  Demultiplexer #(.select(2)) demultiplexer_2 (
    .out0(RA_MBLD), .out1(RB_MBLD), .out2(RC_MBLD), .out3(RD_MBLD), .in(ALU_DISP), .sel(MB_INST));
  Pull_Resistor pull_resistor_1 (.node(pull_resistor_1_node));
  assign pull_resistor_1_node = demultiplexer_1_out1 ? TXB_INST[5:0] : 6'bz;  // Controlled_Buffer controlled_buffer_1
  Pull_Resistor pull_resistor_2 (.node(pull_resistor_2_node));
  assign pull_resistor_2_node = demultiplexer_1_out2 ? TXB_INST[5:0] : 6'bz;  // Controlled_Buffer controlled_buffer_2
  Pull_Resistor pull_resistor_3 (.node(pull_resistor_3_node));
  assign pull_resistor_3_node = demultiplexer_1_out3 ? TXB_INST[5:0] : 6'bz;  // Controlled_Buffer controlled_buffer_3
  Pull_Resistor pull_resistor_4 (.node(pull_resistor_4_node));
  assign pull_resistor_4_node = demultiplexer_1_out0 ? TXB_INST[5:0] : 6'bz;  // Controlled_Buffer controlled_buffer_4
  Demultiplexer #(.select(3)) demultiplexer_3 (
    .out0(demultiplexer_3_out0), .out1(demultiplexer_3_out1), .out2(demultiplexer_3_out2),
    .out3(demultiplexer_3_out3), .out4(FG_LD), .out5(MB_LD), .out6(ST_PUSH), .in(1'b1),
    .sel(pull_resistor_1_node[2:0]));  // open: out7
  Demultiplexer #(.select(3)) demultiplexer_4 (
    .out0(demultiplexer_4_out0), .out1(demultiplexer_4_out1), .out2(demultiplexer_4_out2),
    .out3(demultiplexer_4_out3), .out4(FG_EN), .out5(MB_EN), .out6(ST_POP), .in(1'b1),
    .sel(pull_resistor_1_node[5:3]));  // open: out7
  Demultiplexer #(.select(2)) demultiplexer_5 (
    .out0(demultiplexer_5_out0), .out1(demultiplexer_5_out1), .out2(TX_LOAD), .out3(ST_PUSH), .in(1'b1),
    .sel(pull_resistor_2_node[3:2]));
  Demultiplexer #(.select(2)) demultiplexer_6 (
    .out0(demultiplexer_6_out0), .out1(demultiplexer_6_out1), .out2(TX_OTXB), .out3(ST_POP), .in(1'b1),
    .sel(pull_resistor_2_node[5:4]));
  Demultiplexer #(.select(2)) demultiplexer_7 (
    .in(1'b1), .sel(pull_resistor_3_node[3:2]));  // open: out0, out1, out2, out3
  Demultiplexer #(.select(2)) demultiplexer_8 (
    .in(1'b1), .sel(pull_resistor_3_node[5:4]));  // open: out0, out1, out2, out3
  Demultiplexer #(.select(2)) demultiplexer_9 (
    .out0(demultiplexer_9_out0), .out1(demultiplexer_9_out1), .out2(demultiplexer_9_out2),
    .out3(demultiplexer_9_out3), .in(1'b1), .sel(pull_resistor_4_node[4:3]));
  Demultiplexer #(.select(2)) demultiplexer_10 (
    .out0(demultiplexer_10_out0), .out1(demultiplexer_10_out1), .out2(demultiplexer_10_out2),
    .out3(demultiplexer_10_out3), .in(1'b1), .sel(pull_resistor_4_node[2:1]));
  assign controlled_buffer_5_out = demultiplexer_1_out1 ? demultiplexer_3_out0 : 1'bz;  // Controlled_Buffer controlled_buffer_5
  assign controlled_buffer_6_out = demultiplexer_1_out1 ? demultiplexer_4_out0 : 1'bz;  // Controlled_Buffer controlled_buffer_6
  assign controlled_buffer_7_out = demultiplexer_1_out2 ? demultiplexer_5_out0 : 1'bz;  // Controlled_Buffer controlled_buffer_7
  assign controlled_buffer_8_out = demultiplexer_1_out2 ? demultiplexer_6_out0 : 1'bz;  // Controlled_Buffer controlled_buffer_8
  and and_1 (and_1_out, pull_resistor_4_node[5], demultiplexer_1_out0);
  Pull_Resistor pull_resistor_5 (.node(controlled_buffer_5_out));
  Pull_Resistor pull_resistor_6 (.node(controlled_buffer_6_out));
  or or_1 (or_1_out, controlled_buffer_5_out, controlled_buffer_6_out);
  or or_2 (or_2_out, controlled_buffer_7_out, controlled_buffer_8_out);
  Pull_Resistor pull_resistor_7 (.node(controlled_buffer_7_out));
  Pull_Resistor pull_resistor_8 (.node(controlled_buffer_8_out));
  and and_2 (and_2_out, and_1_out, demultiplexer_9_out0);
  and and_3 (and_3_out, and_1_out, demultiplexer_10_out0);
  or or_3 (or_3_out, demultiplexer_3_out1, demultiplexer_4_out1);
  or or_4 (or_4_out, demultiplexer_3_out2, demultiplexer_4_out2);
  or or_5 (or_5_out, demultiplexer_5_out1, demultiplexer_6_out1);
  or or_6 (or_6_out, demultiplexer_3_out3, demultiplexer_4_out3);
  or or_7 (RA_TXLD, controlled_buffer_5_out, controlled_buffer_7_out);
  or or_8 (RB_TXLD, demultiplexer_3_out1, controlled_buffer_7_out);
  or or_9 (or_9_out, controlled_buffer_7_out, controlled_buffer_8_out);
  or or_10 (RC_TXLD, demultiplexer_3_out2, demultiplexer_5_out1);
  or or_11 (RD_TXLD, demultiplexer_3_out3, demultiplexer_5_out1);
  or or_12 (or_12_out, demultiplexer_5_out1, demultiplexer_6_out1);
  or or_13 (RA_TL, or_1_out, and_2_out);
  or or_14 (RB_TL, or_3_out, demultiplexer_9_out1);
  or or_15 (RC_TL, or_4_out, demultiplexer_9_out2);
  or or_16 (RD_TL, or_6_out, demultiplexer_9_out3);
  or or_17 (RA_TH, or_2_out, and_3_out);
  or or_18 (RB_TH, or_9_out, demultiplexer_10_out1);
  or or_19 (RC_LH, or_5_out, demultiplexer_10_out2);
  or or_20 (RD_TH, or_12_out, demultiplexer_10_out3);

  // Notes on the sheet:
  //   assert to TX
  //   assert to ADDR from TX
endmodule

module PipelineStage0 (
  input  [7:0] INST_IN,
  input  CLOCK,
  input  STALL,
  output [7:0] INST_OUT,
  output PC_OADB,
  output PC_INC,
  output MEM_READ
);

  wire [2:2] not_1_out;

  not not_1 (not_1_out[2], STALL);
  Register register_1 (.D(INST_IN), .en(not_1_out[2]), .clk(CLOCK), .Q(INST_OUT));  // open: clr
  Register #(.width(3)) register_2 (
    .D({3{not_1_out[2]}}), .en(1'b1), .clk(CLOCK), .Q({MEM_READ, PC_INC, PC_OADB}));  // open: clr
endmodule

module PipelineStage1 (
  input  [7:0] INST_IN,
  input  CLOCK,
  input  STALL,
  input  [6:0] FLAGS,
  output [7:0] INST_OUT,
  output STALL_0,
  output PC_INC,
  output MB_LOAD,
  output [7:0] TXB_INST,
  output ALU_DISP,
  output [1:0] MB_INST,
  output [3:0] ALU_INST
);

  wire not_1_out;
  wire [0:0] register_4_q;
  wire [7:0] rom_1_data, rom_2_data, rom_3_data;
  wire [7:3] register_2_q;

  not not_1 (not_1_out, STALL);
  ROM #(.addrWidth(15)) rom_1 (.addr({FLAGS, INST_IN}), .data(rom_1_data));
  ROM #(.addrWidth(15)) rom_2 (.addr({FLAGS, INST_IN}), .data(rom_2_data));
  ROM #(.addrWidth(15)) rom_3 (.addr({FLAGS, INST_IN}), .data(rom_3_data));
  Register register_1 (.D(INST_IN), .en(not_1_out), .clk(CLOCK), .Q(INST_OUT));  // open: clr
  Register register_2 (
    .D(rom_1_data), .en(not_1_out), .clk(CLOCK), .Q({register_2_q, MB_LOAD, PC_INC, STALL_0}));  // open: clr
  Register register_3 (.D(rom_2_data), .en(not_1_out), .clk(CLOCK), .Q(TXB_INST));  // open: clr
  Register register_4 (
    .D(rom_3_data), .en(not_1_out), .clk(CLOCK), .Q({ALU_INST, MB_INST, ALU_DISP, register_4_q[0]}));  // open: clr

  // Notes on the sheet:
  //   contents of rom_2 (hex, n*v repeats v):
  //   64*0 20 28 30 38
  //   contents of rom_3 (hex, n*v repeats v):
  //   64*0 42 46 4a 4e
endmodule
